// Logisim project 03f552f519d7c735.circ as structural Verilog: 1 circuit, main circuit main
module main (
  input  A,
  input  B,
  input  C,
  output out_4
);

  wire and_1_out, multiplexer_1_out, not_1_out, not_2_out, xor_1_out;

  Multiplexer #(.disabled(0), .enable("false")) multiplexer_1 (
    .in0(1'b0), .in1(not_1_out), .out(multiplexer_1_out), .sel(B));
  not not_1 (not_1_out, C);
  not not_2 (not_2_out, B);
  and and_1 (and_1_out, B, C);
  Multiplexer #(.disabled(0), .enable("false")) multiplexer_2 (
    .in0(multiplexer_1_out), .in1(xor_1_out), .out(out_4), .sel(A));
  xor xor_1 (xor_1_out, not_2_out, and_1_out);
endmodule
