// Logisim project 2-ух разрядный умножитель.circ as structural Verilog: 1 circuit, main circuit main
module main (
  input  \А0 ,
  input  \А1 ,
  input  \В0 ,
  input  \В1 ,
  output out_5,
  output out_6,
  output out_7,
  output out_8
);

  wire adder_1_cout, and_2_out, and_3_out, and_4_out;

  and and_1 (out_5, \В0 , \А0 );
  and and_2 (and_2_out, \А0 , \В1 );
  and and_3 (and_3_out, \А1 , \В0 );
  and and_4 (and_4_out, \А1 , \В1 );
  Adder #(.width(1)) adder_1 (.a(and_2_out), .b(and_3_out), .out(out_6), .cout(adder_1_cout));  // open: cin
  Adder #(.width(1)) adder_2 (.a(adder_1_cout), .b(and_4_out), .out(out_7), .cout(out_8));  // open: cin
endmodule
