// Logisim project Г.circ as structural Verilog: 1 circuit, main circuit main
module main (
  input  A_i,
  input  B_i,
  input  A_i_2,
  input  B_i_2,
  input  A_i_3,
  input  B_i_3,
  input  A_i_4,
  input  B_i_4,
  input  A_i_1__B_i_1,
  input  A_i_1__B_i_1_2,
  input  A_i_1__B_i_1_3,
  output A_B,
  output A_B_2,
  output A_B_3
);

  wire and_1_out, and_3_out, and_4_out, and_5_out, and_6_out, and_7_out, and_8_out, and_9_out, and_10_out,
       and_11_out, and_12_out, comparator_1_eq, comparator_1_gt, comparator_1_lt, comparator_2_eq,
       comparator_2_gt, comparator_2_lt, comparator_3_eq, comparator_3_gt, comparator_3_lt, comparator_4_eq,
       comparator_4_gt, comparator_4_lt, or_3_out, or_4_out, or_5_out, or_6_out, or_7_out, or_8_out;

  Comparator #(.width(1)) comparator_1 (
    .a(A_i), .b(B_i), .gt(comparator_1_gt), .eq(comparator_1_eq), .lt(comparator_1_lt));
  Comparator #(.width(1)) comparator_2 (
    .a(A_i_2), .b(B_i_2), .gt(comparator_2_gt), .eq(comparator_2_eq), .lt(comparator_2_lt));
  Comparator #(.width(1)) comparator_3 (
    .a(A_i_3), .b(B_i_3), .gt(comparator_3_gt), .eq(comparator_3_eq), .lt(comparator_3_lt));
  Comparator #(.width(1)) comparator_4 (
    .a(A_i_4), .b(B_i_4), .gt(comparator_4_gt), .eq(comparator_4_eq), .lt(comparator_4_lt));
  and and_1 (and_1_out, comparator_1_gt, and_5_out);
  and and_2 (A_B_2, comparator_1_eq, and_5_out);
  and and_3 (and_3_out, comparator_1_lt, and_5_out);
  and and_4 (and_4_out, comparator_2_gt, and_8_out);
  and and_5 (and_5_out, comparator_2_eq, and_8_out);
  and and_6 (and_6_out, comparator_2_lt, and_8_out);
  and and_7 (and_7_out, comparator_3_gt, and_11_out);
  and and_8 (and_8_out, comparator_3_eq, and_11_out);
  and and_9 (and_9_out, comparator_3_lt, and_11_out);
  and and_10 (and_10_out, comparator_4_gt, A_i_1__B_i_1_2);
  and and_11 (and_11_out, comparator_4_eq, A_i_1__B_i_1_2);
  and and_12 (and_12_out, comparator_4_lt, A_i_1__B_i_1_2);
  or or_1 (A_B, or_3_out, and_1_out);
  or or_2 (A_B_3, and_3_out, or_4_out);
  or or_3 (or_3_out, or_5_out, and_4_out);
  or or_4 (or_4_out, and_6_out, or_6_out);
  or or_5 (or_5_out, or_7_out, and_7_out);
  or or_6 (or_6_out, and_9_out, or_8_out);
  or or_7 (or_7_out, A_i_1__B_i_1_3, and_10_out);
  or or_8 (or_8_out, and_12_out, A_i_1__B_i_1);
endmodule
