// Logisim project Двухступенчатый D-триггер.circ as structural Verilog: 1 circuit, main circuit main
module main (
  input  Not_S,
  input  D,
  input  \С ,
  input  Not_R,
  output out_5,
  output out_6
);

  wire nand_1_out, nand_2_out, nand_3_out, nand_4_out, nand_5_out, nand_6_out, not_1_out;

  nand nand_1 (nand_1_out, D, \С );
  nand nand_2 (nand_2_out, nand_1_out, \С );
  not not_1 (not_1_out, \С );
  nand nand_3 (nand_3_out, nand_1_out, Not_S, nand_4_out);
  nand nand_4 (nand_4_out, nand_3_out, Not_R, nand_2_out);
  nand nand_5 (nand_5_out, nand_3_out, not_1_out);
  nand nand_6 (nand_6_out, nand_5_out, not_1_out);
  LED Q (.in(out_5));
  nand nand_7 (out_5, nand_5_out, Not_S, out_6);
  LED Not_Q (.in(out_6));
  nand nand_8 (out_6, out_5, Not_R, nand_6_out);
endmodule
