// Logisim project М.circ as structural Verilog: 1 circuit, main circuit main
module main (
  input  A,
  input  B,
  input  C,
  output out_4
);

  wire multiplexer_1_out, not_2_out;

  // NOT_Gate not_1 is placed but not wired
  Multiplexer #(.disabled(0), .enable("false")) multiplexer_1 (
    .in0(1'b0), .in1(not_2_out), .out(multiplexer_1_out), .sel(B));
  not not_2 (not_2_out, C);
  Multiplexer #(.disabled(0), .enable("false")) multiplexer_2 (
    .in0(multiplexer_1_out), .out(out_4), .sel(A));  // open: in1
endmodule
