// Logisim project Модифицированный одноразрядный компаратор.circ as structural Verilog: 1 circuit, main circuit main
module main (
  input  A_i,
  input  B_i,
  input  A_i_1__B_i_1,
  input  A_i_1__B_i_1_2,
  input  A_i_1__B_i_1_3,
  output A_B,
  output A_B_2,
  output A_B_3
);

  wire and_1_out, and_3_out, comparator_1_eq, comparator_1_gt, comparator_1_lt;

  Comparator #(.width(1)) comparator_1 (
    .a(A_i), .b(B_i), .gt(comparator_1_gt), .eq(comparator_1_eq), .lt(comparator_1_lt));
  or or_1 (A_B, A_i_1__B_i_1_3, and_1_out);
  and and_1 (and_1_out, comparator_1_gt, A_i_1__B_i_1_2);
  and and_2 (A_B_2, comparator_1_eq, A_i_1__B_i_1_2);
  and and_3 (and_3_out, comparator_1_lt, A_i_1__B_i_1_2);
  or or_2 (A_B_3, and_3_out, A_i_1__B_i_1);
endmodule
