// Logisim project Накапливающий сумматор.circ as structural Verilog: 1 circuit, main circuit main
module main (
  input  Cin,
  input  [3:0] A,
  input  [3:0] B,
  input  R,
  output Cout
);

  wire C_out;
  wire [3:0] adder_1_out, register_1_q;
  wire [4:4] adder_1_cout;

  Clock C (.out(C_out));
  Adder #(.width(4)) adder_1 (.a(A), .b(B), .out(adder_1_out), .cin(Cin), .cout(adder_1_cout[4]));
  Register #(.width(5)) register_1 (
    .D({adder_1_cout[4], adder_1_out}), .en(1'b1), .Q({Cout, register_1_q}), .clk(C_out), .clr(R));
  Hex_Digit_Display hex_digit_display_1 (.value(register_1_q));  // open: dp
endmodule
