// Logisim project Одноступенчатый D-триггер, выполненный на элементах И-НЕ, упр. вариант.circ as structural Verilog: 1 circuit, main circuit main
module main (
  input  D,
  input  C,
  output Q,
  output Not_Q
);

  wire nand_1_out, nand_2_out;

  nand nand_1 (nand_1_out, D, C);
  nand nand_2 (nand_2_out, C, nand_1_out);
  LED led_1 (.in(Q));
  nand nand_3 (Q, nand_1_out, Not_Q);
  nand nand_4 (Not_Q, Q, nand_2_out);
  LED led_2 (.in(Not_Q));
endmodule
