// Logisim project Одноступенчатый D-триггер, выполненный на элементах И-НЕ.circ as structural Verilog: 1 circuit, main circuit main
module main (
  input  D,
  input  C,
  output Q,
  output Not_Q
);

  wire nand_1_out, nand_2_out, nand_3_out;

  nand nand_1 (nand_1_out, D, D);
  nand nand_2 (nand_2_out, D, C);
  nand nand_3 (nand_3_out, C, nand_1_out);
  LED led_1 (.in(Q));
  nand nand_4 (Q, nand_2_out, Not_Q);
  LED led_2 (.in(Not_Q));
  nand nand_5 (Not_Q, Q, nand_3_out);
endmodule
