// Logisim project Одноступенчатый RS-триггер, с динамической синхронизацией, выполненный на элементах И-НЕ.circ as structural Verilog: 1 circuit, main circuit main
module main (
  input  Not_S,
  input  C,
  input  Not_R,
  output Q,
  output Not_Q
);

  wire nand_1_out, nand_2_out, nand_3_out, nand_4_out;

  nand nand_1 (nand_1_out, nand_3_out, Not_S);
  nand nand_2 (nand_2_out, Not_R, nand_4_out);
  nand nand_3 (nand_3_out, nand_1_out, C, nand_4_out);
  nand nand_4 (nand_4_out, nand_3_out, C, nand_2_out);
  nand nand_5 (Q, nand_3_out, Not_Q);
  nand nand_6 (Not_Q, Q, nand_4_out);
  LED led_1 (.in(Q));
  LED led_2 (.in(Not_Q));
endmodule
