// Logisim project Одноступенчатый синхронный RS-триггер на элементах И-НЕ.circ as structural Verilog: 1 circuit, main circuit main
module main (
  input  S,
  input  C,
  input  R,
  output Q,
  output not_Q
);

  wire nand_1_out, nand_2_out;

  nand nand_1 (nand_1_out, S, C);
  nand nand_2 (nand_2_out, C, R);
  nand nand_3 (Q, nand_1_out, not_Q);
  nand nand_4 (not_Q, Q, nand_2_out);
  LED led_1 (.in(Q));
  LED led_2 (.in(not_Q));
endmodule
