// Logisim project П-К.circ as structural Verilog: 1 circuit, main circuit main
module main (
  input  [2:0] in_1
);

  wire decoder_1_out0, decoder_1_out1, decoder_1_out2, decoder_1_out3, decoder_1_out4, decoder_1_out5,
       decoder_1_out6, decoder_1_out7, or_1_out, or_2_out, or_3_out;
  wire [0:0] or_4_out;
  wire [2:0] priority_encoder_1_out;

  Decoder #(.select(3), .disabled(0), .enable("false")) decoder_1 (
    .out0(decoder_1_out0), .out1(decoder_1_out1), .out2(decoder_1_out2), .out3(decoder_1_out3),
    .out4(decoder_1_out4), .out5(decoder_1_out5), .out6(decoder_1_out6), .out7(decoder_1_out7), .sel(in_1));
  or or_1 (or_1_out, decoder_1_out0, decoder_1_out5);
  or or_2 (or_2_out, decoder_1_out1, decoder_1_out6);
  or or_3 (or_3_out, decoder_1_out2, decoder_1_out7);
  Priority_Encoder priority_encoder_1 (
    .in0(or_1_out), .in1(or_2_out), .in2(or_3_out), .in3(decoder_1_out3), .in4(decoder_1_out4),
    .out(priority_encoder_1_out));  // open: in5, in6, in7, en_in, gs, en_out
  Hex_Digit_Display hex_digit_display_1 (.value({3'b000, or_4_out[0]}));  // open: dp
  or or_4 (or_4_out[0], decoder_1_out5, decoder_1_out6, decoder_1_out7);
  Hex_Digit_Display hex_digit_display_2 (.value({1'b0, priority_encoder_1_out}));  // open: dp
endmodule
