// Logisim project Полный одноразрядный сумматор.circ as structural Verilog: 1 circuit, main circuit main
module main (
  input  Ci,
  input  A,
  input  B,
  input  Ci_2,
  input  A_2,
  input  B_2,
  output Si,
  output C_i_1,
  output Si_2,
  output C_i_1_2
);

  wire and_1_out, and_2_out, nor_1_out, nor_2_out, nor_3_out, nor_4_out, nor_5_out, nor_6_out, nor_7_out,
       nor_8_out, nor_9_out, nor_10_out, nor_11_out, nor_13_out, xor_1_out;

  nor nor_1 (nor_1_out, A_2, A_2);
  nor nor_2 (nor_2_out, B_2, B_2);
  xor xor_1 (xor_1_out, A, B);
  and and_1 (and_1_out, B, A);
  nor nor_3 (nor_3_out, nor_1_out, nor_2_out);
  nor nor_4 (nor_4_out, nor_3_out, nor_5_out);
  nor nor_5 (nor_5_out, A_2, B_2);
  nor nor_6 (nor_6_out, nor_2_out, nor_1_out);
  xor xor_2 (Si, Ci, xor_1_out);
  and and_2 (and_2_out, xor_1_out, Ci);
  or or_1 (C_i_1, and_2_out, and_1_out);
  nor nor_7 (nor_7_out, Ci_2, Ci_2);
  nor nor_8 (nor_8_out, nor_4_out, nor_4_out);
  nor nor_9 (nor_9_out, nor_7_out, nor_8_out);
  nor nor_10 (nor_10_out, Ci_2, nor_4_out);
  nor nor_11 (nor_11_out, nor_8_out, nor_7_out);
  nor nor_12 (Si_2, nor_9_out, nor_10_out);
  nor nor_13 (nor_13_out, nor_11_out, nor_6_out);
  nor nor_14 (C_i_1_2, nor_13_out, nor_13_out);
endmodule
