// Logisim project Полусумматор.circ as structural Verilog: 1 circuit, main circuit main
module main (
  input  A,
  input  A_2,
  input  B,
  input  A_3,
  input  B_2,
  input  B_3,
  output Q1,
  output Q0,
  output out_9,
  output out_10,
  output out_11,
  output out_12
);

  wire nand_1_out, nand_2_out, nand_3_out, nand_4_out, nand_6_out, nor_1_out, nor_2_out, nor_3_out, nor_4_out;

  and and_1 (Q0, B_3, A);
  xor xor_1 (Q1, A, B_3);
  nor nor_1 (nor_1_out, B, B);
  nor nor_2 (nor_2_out, A_2, A_2);
  nor nor_3 (nor_3_out, nor_1_out, nor_2_out);
  nor nor_4 (nor_4_out, B, A_2);
  nor nor_5 (out_11, nor_2_out, nor_1_out);
  nor nor_6 (out_9, nor_3_out, nor_4_out);
  nand nand_1 (nand_1_out, A_3, nand_2_out);
  nand nand_2 (nand_2_out, B_2, B_2);
  nand nand_3 (nand_3_out, A_3, A_3);
  nand nand_4 (nand_4_out, nand_3_out, B_2);
  nand nand_5 (out_12, nand_6_out, nand_6_out);
  nand nand_6 (nand_6_out, B_2, A_3);
  nand nand_7 (out_10, nand_1_out, nand_4_out);
endmodule
