// Logisim project Реверсивный cчетчик с параллельным переносом.circ as structural Verilog: 1 circuit, main circuit main
module main (
  input  C,
  input  minus_1,
  input  plus_1,
  input  R,
  output CARRY,
  output BREAK
);

  wire and_2_out, and_3_out, and_4_out, and_5_out, and_6_out, and_8_out, or_1_out, or_2_out, or_3_out,
       or_4_out;
  wire [3:0] t_ff_4_q, t_ff_4_qn;

  and and_1 (CARRY, t_ff_4_q[3], t_ff_4_q[2], t_ff_4_q[1], t_ff_4_q[0], plus_1);
  and and_2 (and_2_out, t_ff_4_q[2], t_ff_4_q[1], t_ff_4_q[0], plus_1);
  and and_3 (and_3_out, t_ff_4_q[1], t_ff_4_q[0], plus_1);
  and and_4 (and_4_out, t_ff_4_q[0], plus_1);
  and and_5 (and_5_out, t_ff_4_qn[1], t_ff_4_qn[0], minus_1);
  and and_6 (and_6_out, t_ff_4_qn[0], minus_1);
  and and_7 (BREAK, t_ff_4_qn[3], t_ff_4_qn[2], t_ff_4_qn[1], t_ff_4_qn[0], minus_1);
  and and_8 (and_8_out, t_ff_4_qn[2], t_ff_4_qn[1], t_ff_4_qn[0], minus_1);
  or or_1 (or_1_out, and_8_out, and_2_out);
  or or_2 (or_2_out, and_5_out, and_3_out);
  or or_3 (or_3_out, and_6_out, and_4_out);
  T_Flip_Flop t_ff_1 (.clk(C), .T(or_1_out), .Q(t_ff_4_q[3]), .Qn(t_ff_4_qn[3]), .preset(1'b0), .reset(R), .en(1'b1));
  T_Flip_Flop t_ff_2 (.clk(C), .T(or_2_out), .Q(t_ff_4_q[2]), .Qn(t_ff_4_qn[2]), .preset(1'b0), .reset(R), .en(1'b1));
  T_Flip_Flop t_ff_3 (.clk(C), .T(or_3_out), .Q(t_ff_4_q[1]), .Qn(t_ff_4_qn[1]), .preset(1'b0), .reset(R), .en(1'b1));
  T_Flip_Flop t_ff_4 (.clk(C), .T(or_4_out), .Q(t_ff_4_q[0]), .Qn(t_ff_4_qn[0]), .preset(1'b0), .reset(R), .en(1'b1));
  or or_4 (or_4_out, minus_1, plus_1);
  Hex_Digit_Display hex_digit_display_1 (.value(t_ff_4_q));  // open: dp
endmodule
