// Logisim project Регистр с выбором записи и выдачи информации.circ as structural Verilog: 1 circuit, main circuit main
module main (
  input  C,
  input  \Сдвиг_вправо ,
  input  \Режим ,
  input  R,
  input  E,
  input  \Сдвиг_влево ,
  output out_7
);

  wire multiplexer_1_out, multiplexer_2_out, multiplexer_3_out, multiplexer_4_out;
  wire [3:1] d_ff_3_q;

  D_Flip_Flop d_ff_1 (.clk(C), .D(multiplexer_1_out), .Q(d_ff_3_q[3]), .en(E), .reset(R));  // open: Qn, preset
  Multiplexer #(.disabled(0), .enable("false")) multiplexer_1 (
    .in0(\Сдвиг_вправо ), .in1(d_ff_3_q[2]), .out(multiplexer_1_out), .sel(\Режим ));
  Hex_Digit_Display hex_digit_display_1 (.value({d_ff_3_q, out_7}));  // open: dp
  Multiplexer #(.disabled(0), .enable("false")) multiplexer_2 (
    .in0(d_ff_3_q[3]), .in1(d_ff_3_q[1]), .out(multiplexer_2_out), .sel(\Режим ));
  D_Flip_Flop d_ff_2 (.clk(C), .D(multiplexer_2_out), .Q(d_ff_3_q[2]), .en(E), .reset(R));  // open: Qn, preset
  D_Flip_Flop d_ff_3 (.clk(C), .D(multiplexer_3_out), .Q(d_ff_3_q[1]), .en(E), .reset(R));  // open: Qn, preset
  Multiplexer #(.disabled(0), .enable("false")) multiplexer_3 (
    .in0(d_ff_3_q[2]), .in1(out_7), .out(multiplexer_3_out), .sel(\Режим ));
  D_Flip_Flop d_ff_4 (.clk(C), .D(multiplexer_4_out), .Q(out_7), .en(E), .reset(R));  // open: Qn, preset
  Multiplexer #(.disabled(0), .enable("false")) multiplexer_4 (
    .in0(d_ff_3_q[1]), .in1(\Сдвиг_влево ), .out(multiplexer_4_out), .sel(\Режим ));
endmodule
