// Logisim project Регистр с параллельно-последовательным приемом, и последовательной выдачей, реализующий сдвиг вправо.circ as structural Verilog: 1 circuit, main circuit main
module main (
  input  C,
  input  \Вход ,
  input  \Посл_Паралл ,
  input  R,
  input  E,
  input  D3,
  input  D2,
  input  D1,
  input  D0,
  output \Выход 
);

  wire multiplexer_1_out, multiplexer_2_out, multiplexer_3_out, multiplexer_4_out, Q1_q, Q2_q, Q3_q;

  D_Flip_Flop Q3 (.clk(C), .D(multiplexer_1_out), .Q(Q3_q), .en(E), .reset(R));  // open: Qn, preset
  Multiplexer #(.disabled(0), .enable("false")) multiplexer_1 (
    .in0(\Вход ), .in1(D3), .out(multiplexer_1_out), .sel(\Посл_Паралл ));
  Multiplexer #(.disabled(0), .enable("false")) multiplexer_2 (
    .in0(Q3_q), .in1(D2), .out(multiplexer_2_out), .sel(\Посл_Паралл ));
  D_Flip_Flop Q2 (.clk(C), .D(multiplexer_2_out), .Q(Q2_q), .en(E), .reset(R));  // open: Qn, preset
  D_Flip_Flop Q1 (.clk(C), .D(multiplexer_3_out), .Q(Q1_q), .en(E), .reset(R));  // open: Qn, preset
  Multiplexer #(.disabled(0), .enable("false")) multiplexer_3 (
    .in0(Q2_q), .in1(D1), .out(multiplexer_3_out), .sel(\Посл_Паралл ));
  D_Flip_Flop Q0 (.clk(C), .D(multiplexer_4_out), .Q(\Выход ), .en(E), .reset(R));  // open: Qn, preset
  Multiplexer #(.disabled(0), .enable("false")) multiplexer_4 (
    .in0(Q1_q), .in1(D0), .out(multiplexer_4_out), .sel(\Посл_Паралл ));
endmodule
