// Logisim project Регистр с параллельной записью и выдачей информации.circ as structural Verilog: 1 circuit, main circuit main
module main (
  input  C,
  input  R,
  input  E,
  input  D3,
  input  D2,
  input  D1,
  input  D0,
  output Q3,
  output N_Q3,
  output Q2,
  output N_Q2,
  output Q1,
  output N_Q1,
  output Q0,
  output N_Q0
);

  D_Flip_Flop d_ff_1 (.clk(C), .D(D3), .Q(Q3), .Qn(N_Q3), .en(E), .reset(R));  // open: preset
  D_Flip_Flop d_ff_2 (.clk(C), .D(D2), .Q(Q2), .Qn(N_Q2), .en(E), .reset(R));  // open: preset
  D_Flip_Flop d_ff_3 (.clk(C), .D(D1), .Q(Q1), .Qn(N_Q1), .en(E), .reset(R));  // open: preset
  D_Flip_Flop d_ff_4 (.clk(C), .D(D0), .Q(Q0), .Qn(N_Q0), .en(E), .reset(R));  // open: preset
endmodule
