// Logisim project Регистр с последовательным приемом и выдачей со сдвигом влево.circ as structural Verilog: 1 circuit, main circuit main
module main (
  input  R,
  input  E,
  input  \Вход ,
  output \Выход 
);

  wire C_out, Q0_q, Q1_q, Q2_q;

  Clock C (.out(C_out));
  D_Flip_Flop Q3 (.clk(C_out), .D(Q2_q), .Q(\Выход ), .en(E), .reset(R));  // open: Qn, preset
  D_Flip_Flop Q2 (.clk(C_out), .D(Q1_q), .Q(Q2_q), .en(E), .reset(R));  // open: Qn, preset
  D_Flip_Flop Q1 (.clk(C_out), .D(Q0_q), .Q(Q1_q), .en(E), .reset(R));  // open: Qn, preset
  D_Flip_Flop Q0 (.clk(C_out), .D(\Вход ), .Q(Q0_q), .en(E), .reset(R));  // open: Qn, preset
endmodule
