// Logisim project Собранный мультиплексор 4-1.circ as structural Verilog: 1 circuit, main circuit main
module main (
  input  D0,
  input  D1,
  input  D2,
  input  D3,
  input  A0,
  input  A1,
  input  E,
  output out_8
);

  wire and_1_out, and_2_out, and_3_out, and_4_out, not_1_out, not_2_out;

  not not_1 (not_1_out, A0);
  not not_2 (not_2_out, A1);
  and and_1 (and_1_out, D0, not_1_out, not_2_out, E);
  and and_2 (and_2_out, D1, not_1_out, A1, E);
  and and_3 (and_3_out, D2, A0, not_2_out, E);
  and and_4 (and_4_out, D3, A0, A1, E);
  or or_1 (out_8, and_1_out, and_2_out, and_3_out, and_4_out);
endmodule
