// Logisim project Собранный полный 4ех разрядный сумматор с последовательным переносом.circ as structural Verilog: 1 circuit, main circuit main
module main (
  input  A1,
  input  B1,
  input  Cin,
  input  A0,
  input  B0,
  input  A3,
  input  B3,
  input  A2,
  input  B2,
  output Cout
);

  wire nor_1_out, nor_2_out, nor_3_out, nor_4_out, nor_5_out, nor_6_out, nor_7_out, nor_8_out, nor_9_out,
       nor_10_out, nor_11_out, nor_12_out, nor_13_out, nor_14_out, nor_15_out, nor_16_out, nor_17_out,
       nor_19_out, nor_20_out, nor_21_out, nor_22_out, nor_24_out, nor_25_out, nor_26_out, nor_27_out,
       nor_28_out, nor_29_out, nor_30_out, nor_31_out, nor_32_out, nor_33_out, nor_34_out, nor_35_out,
       nor_36_out, nor_37_out, nor_38_out, nor_39_out, nor_40_out, nor_41_out, nor_42_out, nor_43_out,
       nor_44_out, nor_45_out, nor_47_out, nor_48_out, nor_49_out, nor_50_out, nor_52_out, nor_53_out,
       nor_54_out, nor_55_out;
  wire [3:0] nor_18_out;

  nor nor_1 (nor_1_out, A0, A0);
  nor nor_2 (nor_2_out, B0, B0);
  nor nor_3 (nor_3_out, A2, A2);
  nor nor_4 (nor_4_out, B2, B2);
  nor nor_5 (nor_5_out, nor_1_out, nor_2_out);
  nor nor_6 (nor_6_out, A0, B0);
  nor nor_7 (nor_7_out, nor_2_out, nor_1_out);
  nor nor_8 (nor_8_out, nor_3_out, nor_4_out);
  nor nor_9 (nor_9_out, A2, B2);
  nor nor_10 (nor_10_out, nor_4_out, nor_3_out);
  nor nor_11 (nor_11_out, nor_5_out, nor_6_out);
  nor nor_12 (nor_12_out, nor_8_out, nor_9_out);
  nor nor_13 (nor_13_out, Cin, Cin);
  nor nor_14 (nor_14_out, nor_11_out, nor_11_out);
  nor nor_15 (nor_15_out, nor_55_out, nor_55_out);
  nor nor_16 (nor_16_out, nor_12_out, nor_12_out);
  nor nor_17 (nor_17_out, nor_13_out, nor_14_out);
  nor nor_18 (nor_18_out[0], nor_17_out, nor_19_out);
  nor nor_19 (nor_19_out, Cin, nor_11_out);
  nor nor_20 (nor_20_out, nor_14_out, nor_13_out);
  nor nor_21 (nor_21_out, nor_20_out, nor_7_out);
  nor nor_22 (nor_22_out, nor_15_out, nor_16_out);
  nor nor_23 (nor_18_out[2], nor_22_out, nor_24_out);
  nor nor_24 (nor_24_out, nor_55_out, nor_12_out);
  nor nor_25 (nor_25_out, nor_16_out, nor_15_out);
  nor nor_26 (nor_26_out, nor_25_out, nor_10_out);
  nor nor_27 (nor_27_out, nor_21_out, nor_21_out);
  nor nor_28 (nor_28_out, nor_26_out, nor_26_out);
  nor nor_29 (nor_29_out, A1, A1);
  nor nor_30 (nor_30_out, B1, B1);
  nor nor_31 (nor_31_out, A3, A3);
  nor nor_32 (nor_32_out, B3, B3);
  nor nor_33 (nor_33_out, nor_29_out, nor_30_out);
  nor nor_34 (nor_34_out, A1, B1);
  nor nor_35 (nor_35_out, nor_30_out, nor_29_out);
  nor nor_36 (nor_36_out, nor_31_out, nor_32_out);
  nor nor_37 (nor_37_out, A3, B3);
  nor nor_38 (nor_38_out, nor_32_out, nor_31_out);
  nor nor_39 (nor_39_out, nor_33_out, nor_34_out);
  nor nor_40 (nor_40_out, nor_36_out, nor_37_out);
  nor nor_41 (nor_41_out, nor_27_out, nor_27_out);
  nor nor_42 (nor_42_out, nor_39_out, nor_39_out);
  nor nor_43 (nor_43_out, nor_28_out, nor_28_out);
  nor nor_44 (nor_44_out, nor_40_out, nor_40_out);
  nor nor_45 (nor_45_out, nor_41_out, nor_42_out);
  nor nor_46 (nor_18_out[1], nor_45_out, nor_47_out);
  nor nor_47 (nor_47_out, nor_27_out, nor_39_out);
  nor nor_48 (nor_48_out, nor_42_out, nor_41_out);
  nor nor_49 (nor_49_out, nor_48_out, nor_35_out);
  nor nor_50 (nor_50_out, nor_43_out, nor_44_out);
  nor nor_51 (nor_18_out[3], nor_50_out, nor_52_out);
  nor nor_52 (nor_52_out, nor_28_out, nor_40_out);
  nor nor_53 (nor_53_out, nor_44_out, nor_43_out);
  nor nor_54 (nor_54_out, nor_53_out, nor_38_out);
  Hex_Digit_Display hex_digit_display_1 (.value(nor_18_out));  // open: dp
  nor nor_55 (nor_55_out, nor_49_out, nor_49_out);
  nor nor_56 (Cout, nor_54_out, nor_54_out);
endmodule
