// Logisim project Собранный приоритетный шифратор 4-2.circ as structural Verilog: 1 circuit, main circuit main
module main (
  input  X0,
  input  X1,
  input  X2,
  input  X3,
  output Q1,
  output Q0,
  output R
);

  wire and_1_out, not_1_out;

  not not_1 (not_1_out, X2);
  and and_1 (and_1_out, not_1_out, X1);
  or or_1 (R, X3, X2, X1, X0);
  or or_2 (Q1, X3, X2);
  or or_3 (Q0, and_1_out, X3);
endmodule
