// Logisim project Собранный приоритетный шифратор 8-3.circ as structural Verilog: 1 circuit, main circuit main
module main (
  input  X0,
  input  X1,
  input  X2,
  input  X3,
  input  X4,
  input  X5,
  input  X6,
  input  X7,
  output Q2,
  output Q1,
  output Q0,
  output R
);

  wire and_1_out, and_2_out, and_3_out, not_1_out, not_2_out, not_3_out, not_4_out, not_5_out, not_6_out,
       not_7_out, not_8_out, or_1_out, or_2_out, or_3_out;

  or or_1 (or_1_out, X7, X6, not_1_out);
  not not_1 (not_1_out, X5);
  or or_2 (or_2_out, X7, X6, not_2_out);
  not not_2 (not_2_out, X4);
  or or_3 (or_3_out, X7, X6, X3, X2);
  not not_3 (not_3_out, X6);
  and and_1 (and_1_out, not_3_out, X5);
  not not_4 (not_4_out, X6);
  not not_5 (not_5_out, X4);
  and and_2 (and_2_out, not_4_out, not_5_out, X3);
  not not_6 (not_6_out, X6);
  not not_7 (not_7_out, X4);
  and and_3 (and_3_out, not_6_out, not_7_out, not_8_out, X1);
  not not_8 (not_8_out, X2);
  or or_4 (R, X7, X6, X5, X4, X3, X2, X1, X0);
  or or_5 (Q2, X7, X6, X5, X4);
  and and_4 (Q1, or_1_out, or_2_out, or_3_out);
  or or_6 (Q0, X7, and_1_out, and_2_out, and_3_out);
endmodule
