// Logisim project Собранный шифратор 8-3.circ as structural Verilog: 1 circuit, main circuit main
module main (
  input  X0,
  input  X1,
  input  X2,
  input  X3,
  input  X4,
  input  X5,
  input  X6,
  input  X7,
  output Q2,
  output Q1,
  output Q0
);

  or or_1 (Q2, X4, X5, X6, X7);
  or or_2 (Q1, X2, X3, X6, X7);
  or or_3 (Q0, X1, X3, X5, X7);
endmodule
