// Logisim project Сумматор последовательного действия.circ as structural Verilog: 1 circuit, main circuit main
module main (
  input  [7:0] A,
  input  [7:0] B
);

  wire adder_1_cout, adder_1_out, C_out, d_ff_1_q, or_1_out, or_2_out, shift_register_1_out,
       shift_register_2_out, \З_out ;

  Clock C (.out(C_out));
  or or_1 (or_1_out, \З_out , C_out);
  or or_2 (or_2_out, C_out, \З_out );
  Button \u_З  (.out(\З_out ));
  Shift_Register shift_register_1 (
    .shift(C_out), .in(1'b0), .clk(or_1_out), .out(shift_register_1_out), .load(\З_out ), .d0(A[7]),
    .d1(A[6]), .d2(A[5]), .d3(A[4]), .d4(A[3]), .d5(A[2]), .d6(A[1]), .d7(A[0]));  // open: clr, q0, q1, q2, q3, q4, q5, q6, q7
  Shift_Register shift_register_2 (
    .shift(C_out), .in(1'b0), .clk(or_2_out), .out(shift_register_2_out), .load(\З_out ), .d0(B[7]),
    .d1(B[6]), .d2(B[5]), .d3(B[4]), .d4(B[3]), .d5(B[2]), .d6(B[1]), .d7(B[0]));  // open: clr, q0, q1, q2, q3, q4, q5, q6, q7
  Adder #(.width(1)) adder_1 (
    .a(shift_register_1_out), .b(shift_register_2_out), .out(adder_1_out), .cin(d_ff_1_q), .cout(adder_1_cout));
  D_Flip_Flop d_ff_1 (.clk(C_out), .D(adder_1_cout), .Q(d_ff_1_q), .en(C_out), .reset(\З_out ));  // open: Qn, preset
  Shift_Register #(.length(9)) shift_register_3 (
    .shift(1'b1), .in(adder_1_out), .clk(C_out), .clr(\З_out ));  // open: out, load, d0, q0, d1, q1, d2, q2, d3, q3, d4, q4, d5, q5, d6, q6, d7, q7, d8, q8
endmodule
