// Logisim project Сумматор с условным переносом.circ as structural Verilog: 1 circuit, main circuit main
module main (
  input  [11:0] A,
  input  [11:0] B,
  input  Ci,
  input  A_2,
  input  A_3,
  input  A_4,
  input  B_2,
  input  B_3,
  input  B_4,
  output Cout,
  output [11:0] \Сумма ,
  output out_12,
  output out_13,
  output out_14
);

  wire adder_1_cout, adder_2_cout, adder_3_cout, adder_4_cout, adder_5_cout, and_1_out, and_2_out, and_3_out,
       and_4_out, and_5_out, multiplexer_2_out, or_1_out, or_2_out, or_3_out, or_4_out;
  wire [3:0] adder_2_out, adder_3_out, adder_4_out, adder_5_out;

  Adder #(.width(4)) adder_1 (.a(B[3:0]), .b(A[3:0]), .out(\Сумма [3:0]), .cin(1'b0), .cout(adder_1_cout));
  Adder #(.width(4)) adder_2 (.a(B[7:4]), .b(A[7:4]), .out(adder_2_out), .cin(1'b0), .cout(adder_2_cout));
  Adder #(.width(4)) adder_3 (.a(B[7:4]), .b(A[7:4]), .out(adder_3_out), .cin(1'b1), .cout(adder_3_cout));
  Adder #(.width(4)) adder_4 (.a(B[11:8]), .b(A[11:8]), .out(adder_4_out), .cin(1'b0), .cout(adder_4_cout));
  Adder #(.width(4)) adder_5 (.a(B[11:8]), .b(A[11:8]), .out(adder_5_out), .cin(1'b1), .cout(adder_5_cout));
  Multiplexer #(.width(4), .disabled(0), .enable("false")) multiplexer_1 (
    .in0(adder_2_out), .in1(adder_3_out), .out(\Сумма [7:4]), .sel(adder_1_cout));
  Multiplexer #(.disabled(0), .enable("false")) multiplexer_2 (
    .in0(adder_2_cout), .in1(adder_3_cout), .out(multiplexer_2_out), .sel(adder_1_cout));
  Multiplexer #(.width(4), .disabled(0), .enable("false")) multiplexer_3 (
    .in0(adder_4_out), .in1(adder_5_out), .out(\Сумма [11:8]), .sel(multiplexer_2_out));
  Multiplexer #(.disabled(0), .enable("false")) multiplexer_4 (
    .in0(adder_4_cout), .in1(adder_5_cout), .out(Cout), .sel(multiplexer_2_out));
  Adder #(.width(1)) adder_6 (.a(A_2), .b(B_2), .out(out_12), .cin(Ci));  // open: cout
  and and_1 (and_1_out, A_2, B_2);
  and and_2 (and_2_out, Ci, or_1_out);
  or or_1 (or_1_out, A_2, B_2);
  or or_2 (or_2_out, and_1_out, and_2_out);
  Adder #(.width(1)) adder_7 (.a(A_3), .b(B_3), .out(out_13), .cin(or_2_out));  // open: cout
  and and_3 (and_3_out, B_3, A_3);
  or or_3 (or_3_out, B_3, A_3);
  and and_4 (and_4_out, or_3_out, A_2, B_2);
  and and_5 (and_5_out, or_3_out, or_1_out, Ci);
  or or_4 (or_4_out, and_3_out, and_4_out, and_5_out);
  Adder #(.width(1)) adder_8 (.a(A_4), .b(B_4), .out(out_14), .cin(or_4_out));  // open: cout
endmodule
