// Logisim project Счетчик 0-2-4.circ as structural Verilog: 1 circuit, main circuit main
module main (
);

  wire and_1_out, clock_1_out, clock_2_out, d_ff_1_qn, d_ff_2_qn, or_1_out, t_ff_1_qn;
  wire [2:1] d_ff_2_q, t_ff_2_q;

  Clock clock_1 (.out(clock_1_out));
  or or_1 (or_1_out, t_ff_2_q[2], t_ff_2_q[1]);
  T_Flip_Flop t_ff_1 (
    .clk(clock_1_out), .T(or_1_out), .Q(t_ff_2_q[2]), .Qn(t_ff_1_qn), .en(1'b1));  // open: preset, reset
  T_Flip_Flop t_ff_2 (.clk(clock_1_out), .T(t_ff_1_qn), .Q(t_ff_2_q[1]), .en(1'b1));  // open: Qn, preset, reset
  Hex_Digit_Display hex_digit_display_1 (.value({1'b0, t_ff_2_q, 1'b0}));  // open: dp
  Clock clock_2 (.out(clock_2_out));
  D_Flip_Flop d_ff_1 (
    .clk(clock_2_out), .D(d_ff_2_q[1]), .Q(d_ff_2_q[2]), .Qn(d_ff_1_qn), .en(1'b1));  // open: preset, reset
  and and_1 (and_1_out, d_ff_2_qn, d_ff_1_qn);
  Hex_Digit_Display hex_digit_display_2 (.value({1'b0, d_ff_2_q, 1'b0}));  // open: dp
  D_Flip_Flop d_ff_2 (
    .clk(clock_2_out), .D(and_1_out), .Q(d_ff_2_q[1]), .Qn(d_ff_2_qn), .en(1'b1));  // open: preset, reset
endmodule
