// Logisim project Счетчик с произвольным постоянным модулем счета.circ as structural Verilog: 1 circuit, main circuit main
module main (
  input  in_1,
  input  in_2,
  input  in_3,
  input  in_4,
  input  R
);

  wire and_1_out, clock_1_out, or_1_out, xnor_1_out, xnor_2_out, xnor_3_out, xnor_4_out;
  wire [3:0] t_ff_1_q;

  Hex_Digit_Display hex_digit_display_1 (.value(t_ff_1_q));  // open: dp
  T_Flip_Flop #(.trigger("falling")) t_ff_1 (
    .clk(clock_1_out), .T(1'b1), .Q(t_ff_1_q[0]), .preset(1'b0), .reset(or_1_out), .en(1'b1));  // open: Qn
  Clock clock_1 (.out(clock_1_out));
  or or_1 (or_1_out, R, and_1_out);
  T_Flip_Flop #(.trigger("falling")) t_ff_2 (
    .clk(t_ff_1_q[0]), .T(1'b1), .Q(t_ff_1_q[1]), .preset(1'b0), .reset(or_1_out), .en(1'b1));  // open: Qn
  T_Flip_Flop #(.trigger("falling")) t_ff_3 (
    .clk(t_ff_1_q[1]), .T(1'b1), .Q(t_ff_1_q[2]), .preset(1'b0), .reset(or_1_out), .en(1'b1));  // open: Qn
  T_Flip_Flop #(.trigger("falling")) t_ff_4 (
    .clk(t_ff_1_q[2]), .T(1'b1), .Q(t_ff_1_q[3]), .preset(1'b0), .reset(or_1_out), .en(1'b1));  // open: Qn
  xnor xnor_1 (xnor_1_out, in_1, t_ff_1_q[3]);
  xnor xnor_2 (xnor_2_out, in_2, t_ff_1_q[2]);
  xnor xnor_3 (xnor_3_out, in_3, t_ff_1_q[1]);
  xnor xnor_4 (xnor_4_out, in_4, t_ff_1_q[0]);
  and and_1 (and_1_out, clock_1_out, xnor_4_out, xnor_3_out, xnor_2_out, xnor_1_out);
endmodule
