// Logisim project Счетчик.circ as structural Verilog: 1 circuit, main circuit main
module main (
);

  wire and_1_out, clock_1_out, clock_2_out, d_ff_2_qn, d_ff_3_qn, d_ff_5_qn, or_1_out, xor_1_out;
  wire [2:0] d_ff_3_q;
  wire [2:1] d_ff_5_q;

  D_Flip_Flop d_ff_1 (.clk(clock_1_out), .D(d_ff_3_q[0]), .Q(d_ff_3_q[2]), .en(1'b1));  // open: Qn, preset, reset
  Clock clock_1 (.out(clock_1_out));
  or or_1 (or_1_out, d_ff_2_qn, d_ff_3_q[2]);
  D_Flip_Flop d_ff_2 (
    .clk(clock_1_out), .D(or_1_out), .Q(d_ff_3_q[1]), .Qn(d_ff_2_qn), .en(1'b1));  // open: preset, reset
  and and_1 (and_1_out, d_ff_3_qn, d_ff_3_q[1]);
  Hex_Digit_Display hex_digit_display_1 (.value({1'b0, d_ff_3_q}));  // open: dp
  D_Flip_Flop d_ff_3 (
    .clk(clock_1_out), .D(and_1_out), .Q(d_ff_3_q[0]), .Qn(d_ff_3_qn), .en(1'b1));  // open: preset, reset
  Clock clock_2 (.out(clock_2_out));
  xor xor_1 (xor_1_out, d_ff_5_q[2], d_ff_5_q[1]);
  D_Flip_Flop d_ff_4 (.clk(clock_2_out), .D(xor_1_out), .Q(d_ff_5_q[2]), .en(1'b1));  // open: Qn, preset, reset
  D_Flip_Flop d_ff_5 (
    .clk(clock_2_out), .D(d_ff_5_qn), .Q(d_ff_5_q[1]), .Qn(d_ff_5_qn), .en(1'b1));  // open: preset, reset
  Hex_Digit_Display hex_digit_display_2 (.value({1'b0, d_ff_5_q, 1'b1}));  // open: dp
endmodule
