// Logisim project Счтечик 0-6-2.circ as structural Verilog: 1 circuit, main circuit main
module main (
);

  wire clock_1_out, or_1_out, t_ff_1_qn, t_ff_2_qn;
  wire [2:1] t_ff_2_q;

  Clock clock_1 (.out(clock_1_out));
  or or_1 (or_1_out, t_ff_2_qn, t_ff_2_q[2]);
  T_Flip_Flop t_ff_1 (
    .clk(clock_1_out), .T(or_1_out), .Q(t_ff_2_q[2]), .Qn(t_ff_1_qn), .en(1'b1));  // open: preset, reset
  T_Flip_Flop t_ff_2 (
    .clk(clock_1_out), .T(t_ff_1_qn), .Q(t_ff_2_q[1]), .Qn(t_ff_2_qn), .en(1'b1));  // open: preset, reset
  Hex_Digit_Display hex_digit_display_1 (.value({1'b0, t_ff_2_q, 1'b0}));  // open: dp
endmodule
