// Logisim project Т триггер на основе ДВ D триггера.circ as structural Verilog: 1 circuit, main circuit main
module main (
  input  in_1,
  input  C,
  input  in_3,
  output Q,
  output Not_Q
);

  wire nand_1_out, nand_2_out, nand_3_out, nand_4_out, nand_5_out, nand_6_out, not_1_out;

  nand nand_1 (nand_1_out, Not_Q, C);
  nand nand_2 (nand_2_out, C, nand_1_out);
  not not_1 (not_1_out, C);
  nand nand_3 (nand_3_out, nand_1_out, in_1, nand_4_out);
  nand nand_4 (nand_4_out, nand_3_out, in_3, nand_2_out);
  nand nand_5 (nand_5_out, nand_3_out, not_1_out);
  nand nand_6 (nand_6_out, nand_5_out, not_1_out);
  nand nand_7 (Q, nand_5_out, in_1, Not_Q);
  nand nand_8 (Not_Q, Q, in_3, nand_6_out);
  LED led_1 (.in(Q));
  LED led_2 (.in(Not_Q));
endmodule
