// Logisim project У4 Сдвиговый регистр.circ as structural Verilog: 1 circuit, main circuit У4 Сдвиговый регистр
module \У4_Сдвиговый_регистр  (
  input  C,
  input  \Сдвиг_вправо ,
  input  A0,
  input  A1,
  input  R,
  input  E,
  input  D3,
  input  D2,
  input  D1,
  input  D0,
  input  \Сдвиг_влево ,
  output out_12,
  output out_13,
  output out_14,
  output out_15,
  output \Выход_Q3 ,
  output \Выход_Q0 
);

  wire multiplexer_1_out, multiplexer_2_out, multiplexer_3_out, multiplexer_4_out;

  D_Flip_Flop Q3 (.clk(C), .D(multiplexer_1_out), .Q(out_12), .en(E), .reset(R));  // open: Qn, preset
  Multiplexer #(.select(2), .disabled(0), .enable("false")) multiplexer_1 (
    .in0(out_12), .in1(\Сдвиг_вправо ), .in2(out_13), .in3(D3), .out(multiplexer_1_out), .sel({A1, A0}));
  Multiplexer #(.select(2), .disabled(0), .enable("false")) multiplexer_2 (
    .in0(out_13), .in1(out_12), .in2(out_14), .in3(D2), .out(multiplexer_2_out), .sel({A1, A0}));
  D_Flip_Flop Q2 (.clk(C), .D(multiplexer_2_out), .Q(out_13), .en(E), .reset(R));  // open: Qn, preset
  Multiplexer #(.select(2), .disabled(0), .enable("false")) multiplexer_3 (
    .in0(out_14), .in1(out_13), .in2(out_15), .in3(D1), .out(multiplexer_3_out), .sel({A1, A0}));
  D_Flip_Flop Q1 (.clk(C), .D(multiplexer_3_out), .Q(out_14), .en(E), .reset(R));  // open: Qn, preset
  D_Flip_Flop Q0 (.clk(C), .D(multiplexer_4_out), .Q(out_15), .en(E), .reset(R));  // open: Qn, preset
  Multiplexer #(.select(2), .disabled(0), .enable("false")) multiplexer_4 (
    .in0(out_15), .in1(out_14), .in2(\Сдвиг_влево ), .in3(D0), .out(multiplexer_4_out), .sel({A1, A0}));

  assign \Выход_Q0  = out_15;
  assign \Выход_Q3  = out_12;
endmodule
