// Logisim project Универсальный сдвиговый регистр с индикатором.circ as structural Verilog: 1 circuit, main circuit main
module main (
  input  \Сдвиг_вправо ,
  input  [1:0] \Режим ,
  input  R,
  input  E,
  input  D3,
  input  D2,
  input  D1,
  input  D0,
  input  \Сдвиг_влево ,
  output \Выход_Q3 ,
  output \Выход_Q0 
);

  wire C_out, multiplexer_1_out, multiplexer_2_out, multiplexer_3_out, multiplexer_4_out;
  wire [2:1] Q1_q;

  Clock C (.out(C_out));
  D_Flip_Flop Q3 (.clk(C_out), .D(multiplexer_1_out), .Q(\Выход_Q3 ), .en(E), .reset(R));  // open: Qn, preset
  Multiplexer #(.select(2), .disabled(0), .enable("false")) multiplexer_1 (
    .in0(\Выход_Q3 ), .in1(\Сдвиг_вправо ), .in2(Q1_q[2]), .in3(D3), .out(multiplexer_1_out), .sel(\Режим ));
  Hex_Digit_Display hex_digit_display_1 (.value({\Выход_Q3 , Q1_q, \Выход_Q0 }));  // open: dp
  Multiplexer #(.select(2), .disabled(0), .enable("false")) multiplexer_2 (
    .in0(Q1_q[2]), .in1(\Выход_Q3 ), .in2(Q1_q[1]), .in3(D2), .out(multiplexer_2_out), .sel(\Режим ));
  D_Flip_Flop Q2 (.clk(C_out), .D(multiplexer_2_out), .Q(Q1_q[2]), .en(E), .reset(R));  // open: Qn, preset
  Multiplexer #(.select(2), .disabled(0), .enable("false")) multiplexer_3 (
    .in0(Q1_q[1]), .in1(Q1_q[2]), .in2(\Выход_Q0 ), .in3(D1), .out(multiplexer_3_out), .sel(\Режим ));
  D_Flip_Flop Q1 (.clk(C_out), .D(multiplexer_3_out), .Q(Q1_q[1]), .en(E), .reset(R));  // open: Qn, preset
  D_Flip_Flop Q0 (.clk(C_out), .D(multiplexer_4_out), .Q(\Выход_Q0 ), .en(E), .reset(R));  // open: Qn, preset
  Multiplexer #(.select(2), .disabled(0), .enable("false")) multiplexer_4 (
    .in0(\Выход_Q0 ), .in1(Q1_q[1]), .in2(\Сдвиг_влево ), .in3(D0), .out(multiplexer_4_out), .sel(\Режим ));
endmodule
