// Logisim project нестандартный счетчик.circ as structural Verilog: 1 circuit, main circuit main
module main (
);

  wire clock_1_out, decoder_1_out0, decoder_1_out2, decoder_1_out3, decoder_1_out4, or_1_out;
  wire [2:0] d_ff_3_q, priority_encoder_1_out;

  Clock clock_1 (.out(clock_1_out));
  D_Flip_Flop d_ff_1 (
    .clk(clock_1_out), .D(priority_encoder_1_out[2]), .Q(d_ff_3_q[2]), .en(1'b1));  // open: Qn, preset, reset
  Decoder #(.select(3), .disabled(0), .enable("false")) decoder_1 (
    .out0(decoder_1_out0), .out2(decoder_1_out2), .out3(decoder_1_out3), .out4(decoder_1_out4), .sel(d_ff_3_q));  // open: out1, out5, out6, out7
  D_Flip_Flop d_ff_2 (
    .clk(clock_1_out), .D(priority_encoder_1_out[1]), .Q(d_ff_3_q[1]), .en(1'b1));  // open: Qn, preset, reset
  or or_1 (or_1_out, decoder_1_out0, decoder_1_out3);
  Hex_Digit_Display hex_digit_display_1 (.value({1'b0, d_ff_3_q}));  // open: dp
  D_Flip_Flop d_ff_3 (
    .clk(clock_1_out), .D(priority_encoder_1_out[0]), .Q(d_ff_3_q[0]), .en(1'b1));  // open: Qn, preset, reset
  Priority_Encoder #(.disabled(0)) priority_encoder_1 (
    .in2(decoder_1_out4), .in3(decoder_1_out2), .in4(or_1_out), .out(priority_encoder_1_out));  // open: in0, in1, in5, in6, in7, en_in, gs, en_out
  Hex_Digit_Display hex_digit_display_2 (.value(4'b0000));  // open: dp

  // Notes on the sheet:
  //   4 2 3 4
endmodule
