// Logisim project JK-триггер, выполненный по схеме без инвертора.circ as structural Verilog: 1 circuit, main circuit main
module main (
  input  Not_S,
  input  J,
  input  C,
  input  K,
  input  Not_R,
  output Q,
  output not_Q
);

  wire nand_1_out, nand_2_out, nand_3_out, nand_4_out, nand_5_out, nand_6_out;

  nand nand_1 (nand_1_out, not_Q, J, C);
  nand nand_2 (nand_2_out, C, K, Q);
  nand nand_3 (nand_3_out, Not_S, nand_1_out, nand_4_out);
  nand nand_4 (nand_4_out, nand_3_out, nand_2_out, Not_R);
  nand nand_5 (nand_5_out, nand_3_out, nand_1_out, nand_2_out);
  nand nand_6 (nand_6_out, nand_2_out, nand_1_out, nand_4_out);
  nand nand_7 (Q, Not_S, not_Q, nand_5_out);
  nand nand_8 (not_Q, nand_6_out, Q, Not_R);
  LED led_1 (.in(Q));
  LED led_2 (.in(not_Q));
endmodule
