// Logisim project JK-триггер.circ as structural Verilog: 1 circuit, main circuit main
module main (
  input  Not_S,
  input  J,
  input  T,
  input  K,
  input  Not_R,
  output Q,
  output not_Q
);

  wire nand_1_out, nand_2_out, nand_3_out, nand_4_out, nand_5_out, nand_6_out, nand_7_out;

  nand nand_1 (nand_1_out, T, T);
  nand nand_2 (nand_2_out, not_Q, J, nand_1_out);
  nand nand_3 (nand_3_out, nand_1_out, K, Q);
  nand nand_4 (nand_4_out, nand_2_out, Not_S, nand_5_out);
  nand nand_5 (nand_5_out, nand_4_out, Not_R, nand_3_out);
  nand nand_6 (nand_6_out, nand_4_out, T);
  nand nand_7 (nand_7_out, T, nand_5_out);
  LED led_1 (.in(Q));
  nand nand_8 (Q, nand_6_out, Not_S, not_Q);
  nand nand_9 (not_Q, Q, Not_R, nand_7_out);
  LED led_2 (.in(not_Q));
endmodule
