// Logisim project Двухступенчатый синхронный RS-триггер с асинхронными входами предустановки, выполненный на элементах И-НЕ.circ as structural Verilog: 1 circuit, main circuit main
module main (
  input  Not_S,
  input  S,
  input  C,
  input  R,
  input  Not_R,
  output Q,
  output not_Q
);

  wire nand_1_out, nand_2_out, nand_3_out, nand_4_out, nand_5_out, nand_6_out, nand_7_out;

  nand nand_1 (nand_1_out, C, C);
  nand nand_2 (nand_2_out, S, nand_1_out);
  nand nand_3 (nand_3_out, nand_1_out, R);
  nand nand_4 (nand_4_out, nand_2_out, Not_S, nand_5_out);
  nand nand_5 (nand_5_out, nand_4_out, Not_R, nand_3_out);
  nand nand_6 (nand_6_out, nand_4_out, C);
  nand nand_7 (nand_7_out, C, nand_5_out);
  LED led_1 (.in(Q));
  nand nand_8 (Q, nand_6_out, Not_S, not_Q);
  nand nand_9 (not_Q, Q, Not_R, nand_7_out);
  LED led_2 (.in(not_Q));
endmodule
