// Logisim project Динамический RS-триггер, работающий по заднему фронту, выполненный на элементах ИЛИ-НЕ.circ as structural Verilog: 1 circuit, main circuit main
module main (
  input  Not_S,
  input  C,
  input  Not_R,
  output out_4,
  output Not_Q
);

  wire nor_1_out, nor_2_out, nor_3_out, nor_4_out;

  nor nor_1 (nor_1_out, Not_S, nor_3_out);
  nor nor_2 (nor_2_out, nor_4_out, Not_R);
  nor nor_3 (nor_3_out, nor_4_out, nor_1_out, C);
  nor nor_4 (nor_4_out, C, nor_2_out, nor_3_out);
  nor nor_5 (out_4, nor_3_out, Not_Q);
  LED led_1 (.in(out_4));
  nor nor_6 (Not_Q, out_4, nor_4_out);
  LED led_2 (.in(Not_Q));

  // Notes on the sheet:
  //   Q
endmodule
