// Logisim project Одноступенчатый асинхронный RS-триггер на элементах  И-НЕ.circ as structural Verilog: 1 circuit, main circuit main
module main (
  input  Not_R,
  input  Not_S,
  output Q,
  output Not_Q
);

  nand nand_1 (Q, Not_R, Not_Q);
  nand nand_2 (Not_Q, Q, Not_S);
  LED led_1 (.in(Q));
  LED led_2 (.in(Not_Q));
endmodule
