// Logisim project Одноступенчатый асинхронный RS-триггер на элементах ИЛИ-НЕ.circ as structural Verilog: 1 circuit, main circuit main
module main (
  input  R,
  input  S,
  output Q,
  output Not_Q
);

  nor nor_1 (Q, R, Not_Q);
  nor nor_2 (Not_Q, Q, S);
  LED led_1 (.in(Q));
  LED led_2 (.in(Not_Q));
endmodule
