// Logisim project Семен.circ as structural Verilog: 1 circuit, main circuit main
module main (
);

  wire and_1_out, C_out, t_ff_1_qn, t_ff_2_q;
  wire [2:1] xor_1_out;

  Clock C (.out(C_out));
  and and_1 (and_1_out, t_ff_2_q, t_ff_1_qn);
  T_Flip_Flop t_ff_1 (
    .clk(C_out), .T(1'b1), .Q(xor_1_out[2]), .Qn(t_ff_1_qn), .preset(and_1_out), .en(1'b1));  // open: reset
  T_Flip_Flop t_ff_2 (.clk(C_out), .T(xor_1_out[2]), .Q(t_ff_2_q), .preset(and_1_out), .en(1'b1));  // open: Qn, reset
  Hex_Digit_Display hex_digit_display_1 (.value({1'b0, xor_1_out, 1'b1}));  // open: dp
  xor xor_1 (xor_1_out[1], t_ff_2_q, t_ff_1_qn);
endmodule
