// Logisim project Собранный дешифратор 2-4 И.circ as structural Verilog: 1 circuit, main circuit main
module main (
  input  A0,
  input  A1,
  input  E,
  output out_4,
  output out_5,
  output out_6,
  output out_7
);

  wire not_1_out, not_2_out;

  not not_1 (not_1_out, A0);
  not not_2 (not_2_out, A1);
  and and_1 (out_4, not_1_out, not_2_out, E);
  and and_2 (out_5, A0, not_2_out, E);
  and and_3 (out_6, not_1_out, A1, E);
  and and_4 (out_7, A0, A1, E);
endmodule
