// Logisim project Собранный дешифратор 2-4 ИЛИ-НЕ.circ as structural Verilog: 1 circuit, main circuit main
module main (
  input  A0,
  input  A1,
  input  Not_E,
  output out_4,
  output out_5,
  output out_6,
  output out_7
);

  wire not_1_out, not_2_out;

  not not_1 (not_1_out, A0);
  not not_2 (not_2_out, A1);
  nor nor_1 (out_4, A0, A1, Not_E);
  nor nor_2 (out_5, not_1_out, A1, Not_E);
  nor nor_3 (out_6, A0, not_2_out, Not_E);
  nor nor_4 (out_7, not_1_out, not_2_out, Not_E);
endmodule
