// Logisim project Счетчик 0-6-2.circ as structural Verilog: 1 circuit, main circuit main
module main (
);

  wire and_1_out, C_out, t_ff_1_qn, t_ff_2_qn;
  wire [2:1] t_ff_2_q;

  Clock C (.out(C_out));
  T_Flip_Flop t_ff_1 (
    .clk(C_out), .T(1'b1), .Q(t_ff_2_q[2]), .Qn(t_ff_1_qn), .reset(and_1_out), .en(1'b1));  // open: preset
  and and_1 (and_1_out, t_ff_2_q[2], t_ff_2_qn);
  Hex_Digit_Display hex_digit_display_1 (.value({1'b0, t_ff_2_q, 1'b0}));  // open: dp
  T_Flip_Flop t_ff_2 (.clk(C_out), .T(t_ff_1_qn), .Q(t_ff_2_q[1]), .Qn(t_ff_2_qn), .en(1'b1));  // open: preset, reset
endmodule
