// Logisim project Счетчик с параллельным переносом.circ as structural Verilog: 1 circuit, main circuit main
module main (
  input  C,
  input  T,
  input  R,
  output CARRY
);

  wire and_2_out, and_3_out, and_4_out;
  wire [3:0] t_ff_4_q;

  and and_1 (CARRY, t_ff_4_q[3], t_ff_4_q[2], t_ff_4_q[1], t_ff_4_q[0], T);
  and and_2 (and_2_out, t_ff_4_q[2], t_ff_4_q[1], t_ff_4_q[0], T);
  and and_3 (and_3_out, t_ff_4_q[1], t_ff_4_q[0], T);
  and and_4 (and_4_out, t_ff_4_q[0], T);
  T_Flip_Flop t_ff_1 (.clk(C), .T(and_2_out), .Q(t_ff_4_q[3]), .preset(1'b0), .reset(R), .en(1'b1));  // open: Qn
  T_Flip_Flop t_ff_2 (.clk(C), .T(and_3_out), .Q(t_ff_4_q[2]), .preset(1'b0), .reset(R), .en(1'b1));  // open: Qn
  T_Flip_Flop t_ff_3 (.clk(C), .T(and_4_out), .Q(t_ff_4_q[1]), .preset(1'b0), .reset(R), .en(1'b1));  // open: Qn
  T_Flip_Flop t_ff_4 (.clk(C), .T(T), .Q(t_ff_4_q[0]), .preset(1'b0), .reset(R), .en(1'b1));  // open: Qn
  Hex_Digit_Display hex_digit_display_1 (.value(t_ff_4_q));  // open: dp
endmodule
