// Logisim project Счетчик с последовательным переносом.circ as structural Verilog: 1 circuit, main circuit main
module main (
  input  T,
  input  Not_R,
  output out_3,
  output out_4,
  output Q,
  output not_Q
);

  wire nand_1_out, nand_2_out, nand_3_out, nand_4_out, nand_5_out, nand_6_out, nand_7_out, nand_8_out,
       nand_9_out, nand_10_out, nand_11_out, nand_12_out, nand_16_out, nand_17_out, nand_18_out, nand_19_out,
       nand_20_out, nand_21_out, nand_22_out, nand_23_out, nand_24_out, nand_25_out, nand_26_out,
       nand_27_out, nand_28_out, nand_30_out, not_1_out, not_2_out, not_3_out, not_4_out;
  wire [2:0] nand_13_out;

  not not_1 (not_1_out, T);
  not not_2 (not_2_out, out_3);
  nand nand_1 (nand_1_out, out_4, T);
  nand nand_2 (nand_2_out, T, nand_13_out[0]);
  nand nand_3 (nand_3_out, nand_16_out, out_3);
  nand nand_4 (nand_4_out, out_3, nand_13_out[2]);
  nand nand_5 (nand_5_out, nand_1_out, 1'b1, nand_6_out);
  nand nand_6 (nand_6_out, nand_5_out, Not_R, nand_2_out);
  nand nand_7 (nand_7_out, nand_3_out, 1'b1, nand_8_out);
  nand nand_8 (nand_8_out, nand_7_out, Not_R, nand_4_out);
  nand nand_9 (nand_9_out, nand_5_out, not_1_out);
  nand nand_10 (nand_10_out, not_1_out, nand_6_out);
  nand nand_11 (nand_11_out, nand_7_out, not_2_out);
  nand nand_12 (nand_12_out, not_2_out, nand_8_out);
  Hex_Digit_Display hex_digit_display_1 (.value({Q, nand_13_out[2], out_3, nand_13_out[0]}));  // open: dp
  nand nand_13 (nand_13_out[0], nand_9_out, 1'b1, out_4);
  nand nand_14 (out_4, nand_13_out[0], Not_R, nand_10_out);
  nand nand_15 (nand_13_out[2], nand_11_out, 1'b1, nand_16_out);
  nand nand_16 (nand_16_out, nand_13_out[2], Not_R, nand_12_out);
  not not_3 (not_3_out, nand_13_out[0]);
  not not_4 (not_4_out, nand_13_out[2]);
  nand nand_17 (nand_17_out, nand_30_out, nand_13_out[0]);
  nand nand_18 (nand_18_out, nand_13_out[0], out_3);
  nand nand_19 (nand_19_out, not_Q, nand_13_out[2]);
  nand nand_20 (nand_20_out, nand_13_out[2], Q);
  nand nand_21 (nand_21_out, nand_17_out, 1'b1, nand_22_out);
  nand nand_22 (nand_22_out, nand_21_out, Not_R, nand_18_out);
  nand nand_23 (nand_23_out, nand_19_out, 1'b1, nand_24_out);
  nand nand_24 (nand_24_out, nand_23_out, Not_R, nand_20_out);
  nand nand_25 (nand_25_out, nand_21_out, not_3_out);
  nand nand_26 (nand_26_out, not_3_out, nand_22_out);
  nand nand_27 (nand_27_out, nand_23_out, not_4_out);
  nand nand_28 (nand_28_out, not_4_out, nand_24_out);
  nand nand_29 (out_3, nand_25_out, 1'b1, nand_30_out);
  nand nand_30 (nand_30_out, out_3, Not_R, nand_26_out);
  nand nand_31 (Q, nand_27_out, 1'b1, not_Q);
  nand nand_32 (not_Q, Q, Not_R, nand_28_out);
  LED led_1 (.in(Q));
  LED led_2 (.in(not_Q));

  // Notes on the sheet:
  //   not Q
endmodule
